// Logisim project fsm.circ as structural Verilog: 1 circuit, main circuit main
module main (
  input  in1,
  input  in2,
  output out
);

  wire and_1_out, and_2_out, and_3_out, and_4_out, and_5_out, and_6_out, and_7_out, and_8_out, and_9_out,
       and_10_out, and_11_out, and_12_out, and_13_out, and_14_out, and_15_out, clk, D0, D1, D2, notInput1,
       notInput2, notQ0, notQ1, notQ2, Q0, Q1, Q2;

  Clock clock_1 (.out(clk));
  not not_1 (notInput1, in1);
  not not_2 (notInput2, in2);
  D_Flip_Flop d_ff_1 (.D(D0), .clk(clk), .Q(Q0), .Qn(notQ0));  // open: preset, reset
  D_Flip_Flop d_ff_2 (.D(D1), .clk(clk), .Q(Q1), .Qn(notQ1));  // open: preset, reset
  D_Flip_Flop d_ff_3 (.D(D2), .clk(clk), .Q(Q2), .Qn(notQ2));  // open: preset, reset
  and and_1 (and_1_out, notQ0, Q1, notQ2);
  or or_1 (out, and_1_out, and_2_out);
  and and_2 (and_2_out, Q0, notQ1, notQ2);
  and and_3 (and_3_out, notQ0, Q1, in2, notInput1);
  and and_4 (and_4_out, notQ0, Q1, in1, notInput2);
  and and_5 (and_5_out, notQ1, notQ2, notInput2, notInput1);
  and and_6 (and_6_out, notQ1, notQ2, in2, in1);
  and and_7 (and_7_out, notQ0, notInput2, notInput1);
  and and_8 (and_8_out, notQ0, in1, in2);
  or or_2 (D0, and_3_out, and_4_out);
  or or_3 (D1, and_5_out, and_6_out, and_7_out, and_8_out);
  and and_9 (and_9_out, notQ0, notQ1, notInput1, in2);
  and and_10 (and_10_out, notQ0, notQ1, in1, notInput2);
  and and_11 (and_11_out, notQ0, Q1, notInput2, notInput1);
  and and_12 (and_12_out, notQ0, Q1, in2, in1);
  and and_13 (and_13_out, notQ0, notQ1, notQ2);
  and and_14 (and_14_out, notQ1, notQ2, in2, notInput1);
  and and_15 (and_15_out, notQ1, notQ2, notInput2, in1);
  or or_4 (D2, and_9_out, and_10_out, and_11_out, and_12_out, and_13_out, and_14_out, and_15_out);

  // Other names for the same wires on the sheet: Input1 = in1; Input2 = in2; Output = out
endmodule
