// Logisim project hw4.circ as structural Verilog: 16 circuits, main circuit main
module main (
  input  reset
);

  wire ALUinB, and_1_out, and_2_out, beq, bgt, branch_signal, clk, DMwe, \input , JP, jr, keyboard_1_avail,
       memory_latch_1_oe_latched, memory_latch_1_we_latched, not_1_out, not_2_out, not_3_out, not_4_out,
       not_zero, \output , Rwe;
  wire [0:0] or_1_out;
  wire [1:0] Rdst, Rwd;
  wire [2:0] ALUop, rd, rs, rt, shamt, write_data;
  wire [3:0] opcode;
  wire [5:0] imm;
  wire [6:0] bit_extender_2_out, keyboard_1_data;
  wire [11:0] addr;
  wire [15:0] A, alu_result, B, bit_extender_3_out, br_target, cur_addr, data_in_mem, extd_imm,
       full_adder_16_bit_4_result, kb_output, memory_latch_1_address_latched, memory_latch_1_data_in_latched,
       multiplexer_3_out, next_addr, next_pc, rd_input, rg0, rg1, rg2, rg3, rg4, rg5, rg6, rg7, rom_1_data,
       temp;

  ROM #(.addrWidth(16), .dataWidth(16)) rom_1 (.addr(cur_addr), .data(rom_1_data));
  register_16_bit register_16_bit_1 (.clk(clk), .in_1(next_pc), .out_5(cur_addr), .enable(1'b1), .reset(reset));
  Multiplexer #(.select(2), .width(16), .enable("false")) multiplexer_1 (
    .in0(next_addr), .in1(br_target), .in2({cur_addr[15:12], addr}), .in3(A), .out(next_pc),
    .sel({JP, or_1_out[0]}));
  or or_1 (or_1_out[0], branch_signal, jr);
  Clock clock_1 (.out(clk));
  full_adder_16_bit full_adder_16_bit_1 (.A(cur_addr), .B(16'h1), .result(next_addr));  // open: ovf, sub
  instruction_decoder instruction_decoder_1 (
    .in_1(rom_1_data), .out_2(rs), .out_3(rt), .out_4(rd), .out_7(imm), .out_6(shamt), .out_8(addr),
    .out_5(opcode), .out_9(ALUop), .out_11(Rwe), .out_13(Rdst), .out_15(ALUinB), .out_10(DMwe), .out_12(Rwd),
    .out_14(JP), .out_16(beq), .out_17(\output ), .out_18(\input ), .out_19(jr), .out_20(bgt));
  assign extd_imm = {{10{imm[5]}}, imm};  // Bit_Extender bit_extender_1
  Multiplexer #(.select(2), .width(3), .enable("false")) multiplexer_2 (
    .in0(rd), .in1(rt), .in2(3'b111), .out(write_data), .sel(Rdst));  // open: in3
  Multiplexer #(.width(16), .enable("false")) multiplexer_3 (
    .in0(B), .in1(extd_imm), .out(multiplexer_3_out), .sel(ALUinB));
  or or_2 (not_zero, alu_result[0], alu_result[1], alu_result[2], alu_result[3], alu_result[4], alu_result[5], alu_result[6], alu_result[7], alu_result[8], alu_result[9], alu_result[10], alu_result[11], alu_result[12], alu_result[13], alu_result[14], alu_result[15]);
  not not_1 (not_1_out, alu_result[15]);
  full_adder_16_bit full_adder_16_bit_2 (.A(16'h1), .B(extd_imm), .result(temp), .sub(1'b0));  // open: ovf
  RegisterFile registerfile_1 (
    .Input(reset), .in_2(write_data), .in_3(not_2_out), .in_4(rs), .in_5(Rwe), .in_6(rt), .in_7(rd_input),
    .out_8(A), .out_9(B), .out_10(rg0), .out_11(rg1), .out_12(rg2), .out_13(rg3), .out_14(rg4), .out_15(rg5),
    .out_16(rg6), .out_17(rg7));
  not not_2 (not_2_out, clk);
  alu alu_1 (.in_3(A), .in_4(multiplexer_3_out), .out_5(alu_result), .Input(shamt), .in_2(ALUop));
  not not_3 (not_3_out, not_zero);
  and and_1 (and_1_out, not_3_out, beq);
  or or_3 (branch_signal, and_1_out, and_2_out);
  and and_2 (and_2_out, not_zero, not_1_out, bgt);
  full_adder_16_bit full_adder_16_bit_3 (.A(cur_addr), .B(temp), .result(br_target), .sub(1'b0));  // open: ovf
  Multiplexer #(.select(2), .width(16), .enable("false")) multiplexer_4 (
    .in0(alu_result), .in1(data_in_mem), .in2(kb_output), .in3(full_adder_16_bit_4_result), .out(rd_input),
    .sel(Rwd));
  Bit_Extender #(.in_width(16), .out_width(7)) bit_extender_2 (.in(A), .out(bit_extender_2_out));
  full_adder_16_bit full_adder_16_bit_4 (
    .A(16'h1), .B(cur_addr), .result(full_adder_16_bit_4_result), .sub(1'b0));  // open: ovf
  not not_4 (not_4_out, clk);
  TTY #(.rows(13), .cols(80), .trigger("falling")) tty_1 (
    .data(bit_extender_2_out), .clk(not_4_out), .we(\output ), .clr(reset));
  Keyboard keyboard_1 (.clk(clk), .re(\input ), .clr(reset), .avail(keyboard_1_avail), .data(keyboard_1_data));
  memory_latch memory_latch_1 (
    .address(alu_result), .WE(DMwe), .clk(clk), .data_in(B),
    .address_latched(memory_latch_1_address_latched), .WE_latched(memory_latch_1_we_latched),
    .OE_latched(memory_latch_1_oe_latched), .data_in_latched(memory_latch_1_data_in_latched));
  RAM #(.addrWidth(16), .dataWidth(16), .trigger("high"), .databus("bibus")) ram_1 (
    .addr(memory_latch_1_address_latched), .we(memory_latch_1_we_latched), .oe(memory_latch_1_oe_latched),
    .din(memory_latch_1_data_in_latched), .dout(data_in_mem));
  assign bit_extender_3_out = {{9{1'b0}}, keyboard_1_data};  // Bit_Extender bit_extender_3
  Multiplexer #(.width(16), .enable("false")) multiplexer_5 (
    .in0(16'h80), .in1(bit_extender_3_out), .out(kb_output), .sel(keyboard_1_avail));

  // Other names for the same wires on the sheet: extd_addr[15:0] = {cur_addr[15:12], addr}

  // Notes on the sheet:
  //   PC
  //   contents of rom_1 (hex, n*v repeats v):
  //   8100 8903 1008 82a0 400 893f 583b 403f
  //   return next addr when clock clicks
  //   00: next_addr
  //   01: branch
  //   10: jump
  //   11: jr
  //   sign_extender
  //   choose if to branch
  //   bgt
  //   register file
  //   ALU
  //   choose rd or rt for return addr 
  //   MSB=0 means positive 
  //   data in rs and rt being input into ALU for operation
  //   setting wrt_en to 1 allows writing to rd
  //   beq
  //   result of ALU operation being input into rd in register file
  //   bgt result cannot be 0
  //   low if result is 0
  //   high if not 0
  //   jal
  //   TYY display
  //   keyboard
  //   does input do anything?
endmodule

module instruction_decoder (
  input  [15:0] in_1,
  output [2:0] out_2,
  output [2:0] out_3,
  output [2:0] out_4,
  output [3:0] out_5,
  output [2:0] out_6,
  output [5:0] out_7,
  output [11:0] out_8,
  output [2:0] out_9,
  output out_10,
  output out_11,
  output [1:0] out_12,
  output [1:0] out_13,
  output out_14,
  output out_15,
  output out_16,
  output out_17,
  output out_18,
  output out_19,
  output out_20
);

  wire add, addi, \and , j, lw, \or , shl, shra, sub;

  or or_1 (out_9[2], shra, shl);
  or or_2 (out_9[1], add, addi, out_16, out_20, sub);
  or or_3 (out_9[0], \and , sub, out_16, out_20, shl);
  or or_4 (out_11, out_18, lw, \or , \and , addi, add, sub, shra, shl, out_13[1]);
  or or_5 (out_13[0], lw, addi);
  Decoder #(.select(4), .enable("false")) decoder_1 (
    .out0(out_17), .out1(out_18), .out2(lw), .out3(out_10), .out4(out_16), .out5(out_20), .out6(\or ),
    .out7(\and ), .out8(addi), .out9(add), .out10(sub), .out11(shra), .out12(shl), .out13(j),
    .out14(out_13[1]), .out15(out_19), .sel(in_1[15:12]));
  or or_6 (out_15, lw, out_10, addi);
  or or_7 (out_14, out_19, out_13[1], j);
  or or_8 (out_12[0], lw, out_13[1]);
  or or_9 (out_12[1], out_18, out_13[1]);

  assign out_2 = in_1[11:9];
  assign out_3 = in_1[8:6];
  assign out_4 = in_1[5:3];
  assign out_5 = in_1[15:12];
  assign out_6 = in_1[2:0];
  assign out_7 = in_1[5:0];
  assign out_8 = in_1[11:0];

  // Other names for the same wires on the sheet: addr[11:0] = in_1[11:0]; instruction[15:0] = in_1;
  //   rt[2:0] = in_1[8:6]; rs[2:0] = in_1[11:9]; ALUinB = out_15; ALUop[2:0] = out_9; beq = out_16; bgt = out_20;
  //   immediate[5:0] = in_1[5:0]; rd[2:0] = in_1[5:3]; input = out_18; JP = out_14; jr = out_19;
  //   opcode[3:0] = in_1[15:12]; output = out_17; Rdst[1:0] = out_13; jal = out_13[1]; Rwd[1:0] = out_12;
  //   Rwe = out_11; shamt[2:0] = in_1[2:0]; DMwe = out_10; sw = out_10

  // Notes on the sheet:
  //   000: OR
  //   011:A-B
  //   101:SHL
  //   OpType: 
  //   001:AND
  //   010: A+B
  //   100:SHRA
  //   00: alu_result
  //   01: data_mem
  //   10: kb_input
  //   11: cur_addr
endmodule

module memory_latch (
  input  [15:0] address,
  input  WE,
  input  clk,
  input  [15:0] data_in,
  output [15:0] address_latched,
  output WE_latched,
  output OE_latched,
  output [15:0] data_in_latched
);

  wire d_ff_1_q;
  wire [15:0] register_1_q;

  Register #(.width(16), .trigger("falling")) register_1 (
    .D(address), .en(WE), .clk(clk), .Q(register_1_q));  // open: clr
  D_Flip_Flop #(.trigger("falling")) d_ff_1 (.D(WE), .clk(clk), .Q(d_ff_1_q));  // open: Qn, preset, reset
  Register #(.width(16), .trigger("falling")) register_2 (
    .D(data_in), .en(WE), .clk(clk), .Q(data_in_latched));  // open: clr
  Multiplexer #(.width(16), .enable("false")) multiplexer_1 (
    .in0(address), .in1(register_1_q), .out(address_latched), .sel(d_ff_1_q));
  and and_1 (WE_latched, clk, d_ff_1_q);
  not not_1 (OE_latched, WE_latched);
endmodule

module RegisterFile (
  input  Input,
  input  [2:0] in_2,
  input  in_3,
  input  [2:0] in_4,
  input  in_5,
  input  [2:0] in_6,
  input  [15:0] in_7,
  output [15:0] out_8,
  output [15:0] out_9,
  output [15:0] out_10,
  output [15:0] out_11,
  output [15:0] out_12,
  output [15:0] out_13,
  output [15:0] out_14,
  output [15:0] out_15,
  output [15:0] out_16,
  output [15:0] out_17
);

  wire first_0, first_1, first_2, first_3, first_4, first_5, first_6, first_7, reg0_reset, regEn1, regEn2,
       regEn3, regEn4, regEn5, regEn6, regEn7, second_0, second_1, second_2, second_3, second_4, second_5,
       second_6, second_7;

  Decoder #(.select(3), .enable("false")) decoder_1 (
    .out0(first_0), .out1(first_1), .out2(first_2), .out3(first_3), .out4(first_4), .out5(first_5),
    .out6(first_6), .out7(first_7), .sel(in_4));
  Decoder #(.select(3)) decoder_2 (
    .out0(reg0_reset), .out1(regEn1), .out2(regEn2), .out3(regEn3), .out4(regEn4), .out5(regEn5),
    .out6(regEn6), .out7(regEn7), .sel(in_2), .en(in_5));
  Decoder #(.select(3), .enable("false")) decoder_3 (
    .out0(second_0), .out1(second_1), .out2(second_2), .out3(second_3), .out4(second_4), .out5(second_5),
    .out6(second_6), .out7(second_7), .sel(in_6));
  assign out_8 = first_0 ? out_10 : 16'bz;  // Controlled_Buffer controlled_buffer_1
  assign out_9 = second_0 ? out_10 : 16'bz;  // Controlled_Buffer controlled_buffer_2
  assign out_8 = first_1 ? out_11 : 16'bz;  // Controlled_Buffer controlled_buffer_3
  assign out_9 = second_1 ? out_11 : 16'bz;  // Controlled_Buffer controlled_buffer_4
  assign out_8 = first_2 ? out_12 : 16'bz;  // Controlled_Buffer controlled_buffer_5
  assign out_9 = second_2 ? out_12 : 16'bz;  // Controlled_Buffer controlled_buffer_6
  assign out_8 = first_3 ? out_13 : 16'bz;  // Controlled_Buffer controlled_buffer_7
  assign out_9 = second_3 ? out_13 : 16'bz;  // Controlled_Buffer controlled_buffer_8
  register_16_bit register_16_bit_1 (.clk(in_3), .in_1(in_7), .out_5(out_10), .enable(reg0_reset), .reset(Input));
  register_16_bit register_16_bit_2 (.clk(in_3), .in_1(in_7), .out_5(out_11), .enable(regEn1), .reset(Input));
  register_16_bit register_16_bit_3 (.clk(in_3), .in_1(in_7), .out_5(out_12), .enable(regEn2), .reset(Input));
  register_16_bit register_16_bit_4 (.clk(in_3), .in_1(in_7), .out_5(out_13), .enable(regEn3), .reset(Input));
  assign out_8 = first_4 ? out_14 : 16'bz;  // Controlled_Buffer controlled_buffer_9
  assign out_9 = second_4 ? out_14 : 16'bz;  // Controlled_Buffer controlled_buffer_10
  // Probe on out_10
  // Probe on out_11
  // Probe on out_12
  // Probe on out_13
  assign out_8 = first_5 ? out_15 : 16'bz;  // Controlled_Buffer controlled_buffer_11
  assign out_9 = second_5 ? out_15 : 16'bz;  // Controlled_Buffer controlled_buffer_12
  register_16_bit register_16_bit_5 (.clk(in_3), .in_1(in_7), .out_5(out_14), .enable(regEn4), .reset(Input));
  register_16_bit register_16_bit_6 (.clk(in_3), .in_1(in_7), .out_5(out_15), .enable(regEn5), .reset(Input));
  register_16_bit register_16_bit_7 (.clk(in_3), .in_1(in_7), .out_5(out_16), .enable(regEn6), .reset(Input));
  register_16_bit register_16_bit_8 (.clk(in_3), .in_1(in_7), .out_5(out_17), .enable(regEn7), .reset(Input));
  assign out_8 = first_6 ? out_16 : 16'bz;  // Controlled_Buffer controlled_buffer_13
  assign out_9 = second_6 ? out_16 : 16'bz;  // Controlled_Buffer controlled_buffer_14
  // Probe on out_14
  // Probe on out_15
  // Probe on out_16
  // Probe on out_17
  assign out_8 = first_7 ? out_17 : 16'bz;  // Controlled_Buffer controlled_buffer_15
  assign out_9 = second_7 ? out_17 : 16'bz;  // Controlled_Buffer controlled_buffer_16

  // Other names for the same wires on the sheet: clk = in_3; enable = in_5; glbreset = Input; input_t[15:0] = in_7;
  //   output0[15:0] = out_10; output1[15:0] = out_11; output2[15:0] = out_12; output3[15:0] = out_13;
  //   output4[15:0] = out_14; output5[15:0] = out_15; output6[15:0] = out_16; output7[15:0] = out_17; Rd[2:0] = in_2;
  //   readdata1[15:0] = out_8; readdata2[15:0] = out_9; Rs[2:0] = in_4; Rt[2:0] = in_6

  // Notes on the sheet:
  //   read logic
  //   write logic
  //   write input to rd
  //   Output
  //   content in register
  //   output=data in register
  //   input=data being written to register
endmodule

module register_16_bit (
  input  [15:0] in_1,
  input  clk,
  input  enable,
  input  reset,
  output [15:0] out_5
);

  wire clk_enable;

  and and_1 (clk_enable, clk, enable);
  D_Flip_Flop d_ff_1 (.D(in_1[3]), .clk(clk_enable), .Q(out_5[3]), .reset(reset));  // open: Qn, preset
  D_Flip_Flop d_ff_2 (.D(in_1[7]), .clk(clk_enable), .Q(out_5[7]), .reset(reset));  // open: Qn, preset
  D_Flip_Flop d_ff_3 (.D(in_1[11]), .clk(clk_enable), .Q(out_5[11]), .reset(reset));  // open: Qn, preset
  D_Flip_Flop d_ff_4 (.D(in_1[15]), .clk(clk_enable), .Q(out_5[15]), .reset(reset));  // open: Qn, preset
  D_Flip_Flop d_ff_5 (.D(in_1[2]), .clk(clk_enable), .Q(out_5[2]), .reset(reset));  // open: Qn, preset
  D_Flip_Flop d_ff_6 (.D(in_1[6]), .clk(clk_enable), .Q(out_5[6]), .reset(reset));  // open: Qn, preset
  D_Flip_Flop d_ff_7 (.D(in_1[10]), .clk(clk_enable), .Q(out_5[10]), .reset(reset));  // open: Qn, preset
  D_Flip_Flop d_ff_8 (.D(in_1[14]), .clk(clk_enable), .Q(out_5[14]), .reset(reset));  // open: Qn, preset
  D_Flip_Flop d_ff_9 (.D(in_1[1]), .clk(clk_enable), .Q(out_5[1]), .reset(reset));  // open: Qn, preset
  D_Flip_Flop d_ff_10 (.D(in_1[5]), .clk(clk_enable), .Q(out_5[5]), .reset(reset));  // open: Qn, preset
  D_Flip_Flop d_ff_11 (.D(in_1[9]), .clk(clk_enable), .Q(out_5[9]), .reset(reset));  // open: Qn, preset
  D_Flip_Flop d_ff_12 (.D(in_1[13]), .clk(clk_enable), .Q(out_5[13]), .reset(reset));  // open: Qn, preset
  D_Flip_Flop d_ff_13 (.D(in_1[0]), .clk(clk_enable), .Q(out_5[0]), .reset(reset));  // open: Qn, preset
  D_Flip_Flop d_ff_14 (.D(in_1[4]), .clk(clk_enable), .Q(out_5[4]), .reset(reset));  // open: Qn, preset
  D_Flip_Flop d_ff_15 (.D(in_1[8]), .clk(clk_enable), .Q(out_5[8]), .reset(reset));  // open: Qn, preset
  D_Flip_Flop d_ff_16 (.D(in_1[12]), .clk(clk_enable), .Q(out_5[12]), .reset(reset));  // open: Qn, preset

  // Other names for the same wires on the sheet: In0 = in_1[0]; In1 = in_1[1]; In2 = in_1[2]; In3 = in_1[3];
  //   In4 = in_1[4]; In5 = in_1[5]; In6 = in_1[6]; In7 = in_1[7]; In8 = in_1[8]; In9 = in_1[9]; In10 = in_1[10];
  //   In11 = in_1[11]; In12 = in_1[12]; In13 = in_1[13]; In14 = in_1[14]; In15 = in_1[15]; R0 = out_5[0];
  //   R1 = out_5[1]; R2 = out_5[2]; R3 = out_5[3]; R4 = out_5[4]; R5 = out_5[5]; R6 = out_5[6]; R7 = out_5[7];
  //   R8 = out_5[8]; R9 = out_5[9]; R10 = out_5[10]; R11 = out_5[11]; R12 = out_5[12]; R13 = out_5[13];
  //   R14 = out_5[14]; R15 = out_5[15]

  // Notes on the sheet:
  //   input
  //   output
  //   (data stored in register)
endmodule

module alu (
  input  [2:0] Input,
  input  [2:0] in_2,
  input  [15:0] in_3,
  input  [15:0] in_4,
  output [15:0] out_5
);

  wire [15:0] add, \and , \or , shl, shra, sub;

  full_adder_16_bit full_adder_16_bit_1 (.A(in_3), .B(in_4), .result(add), .sub(1'b0));  // open: ovf
  assign \or  = in_4 | in_3;  // OR_Gate or_1, 16 bits wide
  full_adder_16_bit full_adder_16_bit_2 (.A(in_3), .B(in_4), .result(sub), .sub(1'b1));  // open: ovf
  assign \and  = in_4 & in_3;  // AND_Gate and_1, 16 bits wide
  shra_barrel shra_barrel_1 (.in_1(Input), .in_2(in_3), .out_3(shra));
  shl_barrel shl_barrel_1 (.in_1(Input), .in_2(in_3), .out_3(shl));
  Multiplexer #(.select(3), .width(16), .enable("false")) multiplexer_1 (
    .in0(\or ), .in1(\and ), .in2(add), .in3(sub), .in4(shra), .in5(shl), .out(out_5), .sel(in_2));  // open: in6, in7

  // Other names for the same wires on the sheet: A[15:0] = in_3; B[15:0] = in_4; OpType[2:0] = in_2;
  //   output[15:0] = out_5; shamt[2:0] = Input

  // Notes on the sheet:
  //   OpType: 
  //   000: OR
  //   001:AND
  //   010: A+B
  //   011:A-B
  //   100:SHRA
  //   101:SHL
  //   Output
  //   make sure each operation is at the correct input position for MUX
endmodule

module full_adder_1_bit (
  input  Cin,
  input  a,
  input  b,
  output Sum,
  output Cout
);

  wire and_1_out, and_2_out, xor_1_out;

  and and_1 (and_1_out, b, a);
  or or_1 (Cout, and_1_out, and_2_out);
  xor xor_1 (xor_1_out, a, b);
  and and_2 (and_2_out, xor_1_out, Cin);
  xor xor_2 (Sum, Cin, xor_1_out);
endmodule

module full_adder_16_bit (
  input  [15:0] A,
  input  [15:0] B,
  input  sub,
  output [15:0] result,
  output ovf
);

  wire full_adder_1_bit_1_cout, full_adder_1_bit_2_cout, full_adder_1_bit_3_cout, full_adder_1_bit_4_cout,
       full_adder_1_bit_5_cout, full_adder_1_bit_6_cout, full_adder_1_bit_7_cout, full_adder_1_bit_8_cout,
       full_adder_1_bit_9_cout, full_adder_1_bit_10_cout, full_adder_1_bit_11_cout, full_adder_1_bit_12_cout,
       full_adder_1_bit_13_cout, full_adder_1_bit_14_cout, full_adder_1_bit_15_cout,
       full_adder_1_bit_16_cout, xor_1_out, xor_3_out, xor_4_out, xor_5_out, xor_6_out, xor_7_out, xor_8_out,
       xor_9_out, xor_10_out, xor_11_out, xor_12_out, xor_13_out, xor_14_out, xor_15_out, xor_16_out,
       xor_17_out;

  xor xor_1 (xor_1_out, sub, B[15]);
  full_adder_1_bit full_adder_1_bit_1 (
    .a(xor_1_out), .b(A[15]), .Cin(full_adder_1_bit_3_cout), .Cout(full_adder_1_bit_1_cout), .Sum(result[15]));
  xor xor_2 (ovf, full_adder_1_bit_1_cout, full_adder_1_bit_3_cout);
  xor xor_3 (xor_3_out, sub, B[13]);
  xor xor_4 (xor_4_out, sub, B[14]);
  full_adder_1_bit full_adder_1_bit_2 (
    .a(xor_3_out), .b(A[13]), .Cin(full_adder_1_bit_5_cout), .Cout(full_adder_1_bit_2_cout), .Sum(result[13]));
  full_adder_1_bit full_adder_1_bit_3 (
    .a(xor_4_out), .b(A[14]), .Cin(full_adder_1_bit_2_cout), .Cout(full_adder_1_bit_3_cout), .Sum(result[14]));
  xor xor_5 (xor_5_out, sub, B[11]);
  xor xor_6 (xor_6_out, sub, B[12]);
  full_adder_1_bit full_adder_1_bit_4 (
    .a(xor_5_out), .b(A[11]), .Cin(full_adder_1_bit_6_cout), .Cout(full_adder_1_bit_4_cout), .Sum(result[11]));
  full_adder_1_bit full_adder_1_bit_5 (
    .a(xor_6_out), .b(A[12]), .Cin(full_adder_1_bit_4_cout), .Cout(full_adder_1_bit_5_cout), .Sum(result[12]));
  xor xor_7 (xor_7_out, sub, B[9]);
  xor xor_8 (xor_8_out, sub, B[10]);
  full_adder_1_bit full_adder_1_bit_6 (
    .a(xor_8_out), .b(A[10]), .Cin(full_adder_1_bit_7_cout), .Cout(full_adder_1_bit_6_cout), .Sum(result[10]));
  full_adder_1_bit full_adder_1_bit_7 (
    .a(xor_7_out), .b(A[9]), .Cin(full_adder_1_bit_9_cout), .Cout(full_adder_1_bit_7_cout), .Sum(result[9]));
  xor xor_9 (xor_9_out, sub, B[7]);
  xor xor_10 (xor_10_out, sub, B[8]);
  full_adder_1_bit full_adder_1_bit_8 (
    .a(xor_9_out), .b(A[7]), .Cin(full_adder_1_bit_10_cout), .Cout(full_adder_1_bit_8_cout), .Sum(result[7]));
  full_adder_1_bit full_adder_1_bit_9 (
    .a(xor_10_out), .b(A[8]), .Cin(full_adder_1_bit_8_cout), .Cout(full_adder_1_bit_9_cout), .Sum(result[8]));
  xor xor_11 (xor_11_out, sub, B[5]);
  xor xor_12 (xor_12_out, sub, B[6]);
  full_adder_1_bit full_adder_1_bit_10 (
    .a(xor_12_out), .b(A[6]), .Cin(full_adder_1_bit_11_cout), .Cout(full_adder_1_bit_10_cout), .Sum(result[6]));
  full_adder_1_bit full_adder_1_bit_11 (
    .a(xor_11_out), .b(A[5]), .Cin(full_adder_1_bit_13_cout), .Cout(full_adder_1_bit_11_cout), .Sum(result[5]));
  xor xor_13 (xor_13_out, sub, B[3]);
  xor xor_14 (xor_14_out, sub, B[4]);
  full_adder_1_bit full_adder_1_bit_12 (
    .a(xor_13_out), .b(A[3]), .Cin(full_adder_1_bit_14_cout), .Cout(full_adder_1_bit_12_cout), .Sum(result[3]));
  full_adder_1_bit full_adder_1_bit_13 (
    .a(xor_14_out), .b(A[4]), .Cin(full_adder_1_bit_12_cout), .Cout(full_adder_1_bit_13_cout), .Sum(result[4]));
  xor xor_15 (xor_15_out, sub, B[1]);
  xor xor_16 (xor_16_out, sub, B[2]);
  full_adder_1_bit full_adder_1_bit_14 (
    .a(xor_16_out), .b(A[2]), .Cin(full_adder_1_bit_15_cout), .Cout(full_adder_1_bit_14_cout), .Sum(result[2]));
  full_adder_1_bit full_adder_1_bit_15 (
    .a(xor_15_out), .b(A[1]), .Cin(full_adder_1_bit_16_cout), .Cout(full_adder_1_bit_15_cout), .Sum(result[1]));
  xor xor_17 (xor_17_out, sub, B[0]);
  full_adder_1_bit full_adder_1_bit_16 (
    .a(xor_17_out), .b(A[0]), .Cin(sub), .Cout(full_adder_1_bit_16_cout), .Sum(result[0]));

  // Other names for the same wires on the sheet: b0 = A[0]; b1 = A[1]; b2 = A[2]; b3 = A[3]; b4 = A[4]; b5 = A[5];
  //   b6 = A[6]; b7 = A[7]; b8 = A[8]; b9 = A[9]; b10 = A[10]; b11 = A[11]; b12 = A[12]; b13 = A[13]; b14 = A[14];
  //   b15 = A[15]; a0 = B[0]; a1 = B[1]; a2 = B[2]; a3 = B[3]; a4 = B[4]; a5 = B[5]; a6 = B[6]; a7 = B[7]; a8 = B[8];
  //   a9 = B[9]; a10 = B[10]; a11 = B[11]; a12 = B[12]; a13 = B[13]; a14 = B[14]; a15 = B[15]

  // Notes on the sheet:
  //   A+B when sub is 0
  //   A-B when sub is 1
endmodule

module shl_1_bit (
  input  [15:0] in_1,
  input  _0_is_to_shift,
  output [15:0] out_3
);

  Multiplexer #(.enable("false")) multiplexer_1 (.in0(1'b0), .in1(in_1[0]), .out(out_3[0]), .sel(_0_is_to_shift));
  Multiplexer #(.enable("false")) multiplexer_2 (.in0(in_1[3]), .in1(in_1[4]), .out(out_3[4]), .sel(_0_is_to_shift));
  Multiplexer #(.enable("false")) multiplexer_3 (.in0(in_1[7]), .in1(in_1[8]), .out(out_3[8]), .sel(_0_is_to_shift));
  Multiplexer #(.enable("false")) multiplexer_4 (.in0(in_1[11]), .in1(in_1[12]), .out(out_3[12]), .sel(_0_is_to_shift));
  Multiplexer #(.enable("false")) multiplexer_5 (.in0(in_1[0]), .in1(in_1[1]), .out(out_3[1]), .sel(_0_is_to_shift));
  Multiplexer #(.enable("false")) multiplexer_6 (.in0(in_1[4]), .in1(in_1[5]), .out(out_3[5]), .sel(_0_is_to_shift));
  Multiplexer #(.enable("false")) multiplexer_7 (.in0(in_1[8]), .in1(in_1[9]), .out(out_3[9]), .sel(_0_is_to_shift));
  Multiplexer #(.enable("false")) multiplexer_8 (.in0(in_1[12]), .in1(in_1[13]), .out(out_3[13]), .sel(_0_is_to_shift));
  Multiplexer #(.enable("false")) multiplexer_9 (.in0(in_1[1]), .in1(in_1[2]), .out(out_3[2]), .sel(_0_is_to_shift));
  Multiplexer #(.enable("false")) multiplexer_10 (.in0(in_1[5]), .in1(in_1[6]), .out(out_3[6]), .sel(_0_is_to_shift));
  Multiplexer #(.enable("false")) multiplexer_11 (.in0(in_1[9]), .in1(in_1[10]), .out(out_3[10]), .sel(_0_is_to_shift));
  Multiplexer #(.enable("false")) multiplexer_12 (
    .in0(in_1[13]), .in1(in_1[14]), .out(out_3[14]), .sel(_0_is_to_shift));
  Multiplexer #(.enable("false")) multiplexer_13 (.in0(in_1[2]), .in1(in_1[3]), .out(out_3[3]), .sel(_0_is_to_shift));
  Multiplexer #(.enable("false")) multiplexer_14 (.in0(in_1[6]), .in1(in_1[7]), .out(out_3[7]), .sel(_0_is_to_shift));
  Multiplexer #(.enable("false")) multiplexer_15 (
    .in0(in_1[10]), .in1(in_1[11]), .out(out_3[11]), .sel(_0_is_to_shift));
  Multiplexer #(.enable("false")) multiplexer_16 (
    .in0(in_1[14]), .in1(in_1[15]), .out(out_3[15]), .sel(_0_is_to_shift));

  // Other names for the same wires on the sheet: in0 = in_1[0]; in1 = in_1[1]; in2 = in_1[2]; in3 = in_1[3];
  //   in4 = in_1[4]; in5 = in_1[5]; in6 = in_1[6]; in7 = in_1[7]; in8 = in_1[8]; in9 = in_1[9]; in10 = in_1[10];
  //   in11 = in_1[11]; in12 = in_1[12]; in13 = in_1[13]; in14 = in_1[14]; in15 = in_1[15]; out0 = out_3[0];
  //   out1 = out_3[1]; out2 = out_3[2]; out3 = out_3[3]; out4 = out_3[4]; out5 = out_3[5]; out6 = out_3[6];
  //   out7 = out_3[7]; out8 = out_3[8]; out9 = out_3[9]; out10 = out_3[10]; out11 = out_3[11]; out12 = out_3[12];
  //   out13 = out_3[13]; out14 = out_3[14]; out15 = out_3[15]; select = _0_is_to_shift

  // Notes on the sheet:
  //   1 is not to shift
endmodule

module shl_2_bit (
  input  [15:0] in_1,
  input  _0_is_to_shift,
  output [15:0] out_3
);

  Multiplexer #(.enable("false")) multiplexer_1 (.in0(1'b0), .in1(in_1[0]), .out(out_3[0]), .sel(_0_is_to_shift));
  Multiplexer #(.enable("false")) multiplexer_2 (.in0(in_1[2]), .in1(in_1[4]), .out(out_3[4]), .sel(_0_is_to_shift));
  Multiplexer #(.enable("false")) multiplexer_3 (.in0(in_1[6]), .in1(in_1[8]), .out(out_3[8]), .sel(_0_is_to_shift));
  Multiplexer #(.enable("false")) multiplexer_4 (.in0(in_1[10]), .in1(in_1[12]), .out(out_3[12]), .sel(_0_is_to_shift));
  Multiplexer #(.enable("false")) multiplexer_5 (.in0(1'b0), .in1(in_1[1]), .out(out_3[1]), .sel(_0_is_to_shift));
  Multiplexer #(.enable("false")) multiplexer_6 (.in0(in_1[3]), .in1(in_1[5]), .out(out_3[5]), .sel(_0_is_to_shift));
  Multiplexer #(.enable("false")) multiplexer_7 (.in0(in_1[7]), .in1(in_1[9]), .out(out_3[9]), .sel(_0_is_to_shift));
  Multiplexer #(.enable("false")) multiplexer_8 (.in0(in_1[11]), .in1(in_1[13]), .out(out_3[13]), .sel(_0_is_to_shift));
  Multiplexer #(.enable("false")) multiplexer_9 (.in0(in_1[0]), .in1(in_1[2]), .out(out_3[2]), .sel(_0_is_to_shift));
  Multiplexer #(.enable("false")) multiplexer_10 (.in0(in_1[4]), .in1(in_1[6]), .out(out_3[6]), .sel(_0_is_to_shift));
  Multiplexer #(.enable("false")) multiplexer_11 (.in0(in_1[8]), .in1(in_1[10]), .out(out_3[10]), .sel(_0_is_to_shift));
  Multiplexer #(.enable("false")) multiplexer_12 (
    .in0(in_1[12]), .in1(in_1[14]), .out(out_3[14]), .sel(_0_is_to_shift));
  Multiplexer #(.enable("false")) multiplexer_13 (.in0(in_1[1]), .in1(in_1[3]), .out(out_3[3]), .sel(_0_is_to_shift));
  Multiplexer #(.enable("false")) multiplexer_14 (.in0(in_1[5]), .in1(in_1[7]), .out(out_3[7]), .sel(_0_is_to_shift));
  Multiplexer #(.enable("false")) multiplexer_15 (.in0(in_1[9]), .in1(in_1[11]), .out(out_3[11]), .sel(_0_is_to_shift));
  Multiplexer #(.enable("false")) multiplexer_16 (
    .in0(in_1[13]), .in1(in_1[15]), .out(out_3[15]), .sel(_0_is_to_shift));

  // Other names for the same wires on the sheet: in0 = in_1[0]; in1 = in_1[1]; in2 = in_1[2]; in3 = in_1[3];
  //   in4 = in_1[4]; in5 = in_1[5]; in6 = in_1[6]; in7 = in_1[7]; in8 = in_1[8]; in9 = in_1[9]; in10 = in_1[10];
  //   in11 = in_1[11]; in12 = in_1[12]; in13 = in_1[13]; in14 = in_1[14]; in15 = in_1[15]; out0 = out_3[0];
  //   out1 = out_3[1]; out2 = out_3[2]; out3 = out_3[3]; out4 = out_3[4]; out5 = out_3[5]; out6 = out_3[6];
  //   out7 = out_3[7]; out8 = out_3[8]; out9 = out_3[9]; out10 = out_3[10]; out11 = out_3[11]; out12 = out_3[12];
  //   out13 = out_3[13]; out14 = out_3[14]; out15 = out_3[15]; select = _0_is_to_shift

  // Notes on the sheet:
  //   1 is not to shift
endmodule

module shl_4_bit (
  input  [15:0] in_1,
  input  _0_is_to_shift,
  output [15:0] out_3
);

  Multiplexer #(.enable("false")) multiplexer_1 (.in0(1'b0), .in1(in_1[0]), .out(out_3[0]), .sel(_0_is_to_shift));
  Multiplexer #(.enable("false")) multiplexer_2 (.in0(in_1[0]), .in1(in_1[4]), .out(out_3[4]), .sel(_0_is_to_shift));
  Multiplexer #(.enable("false")) multiplexer_3 (.in0(in_1[4]), .in1(in_1[8]), .out(out_3[8]), .sel(_0_is_to_shift));
  Multiplexer #(.enable("false")) multiplexer_4 (.in0(in_1[8]), .in1(in_1[12]), .out(out_3[12]), .sel(_0_is_to_shift));
  Multiplexer #(.enable("false")) multiplexer_5 (.in0(1'b0), .in1(in_1[1]), .out(out_3[1]), .sel(_0_is_to_shift));
  Multiplexer #(.enable("false")) multiplexer_6 (.in0(in_1[1]), .in1(in_1[5]), .out(out_3[5]), .sel(_0_is_to_shift));
  Multiplexer #(.enable("false")) multiplexer_7 (.in0(in_1[5]), .in1(in_1[9]), .out(out_3[9]), .sel(_0_is_to_shift));
  Multiplexer #(.enable("false")) multiplexer_8 (.in0(in_1[9]), .in1(in_1[13]), .out(out_3[13]), .sel(_0_is_to_shift));
  Multiplexer #(.enable("false")) multiplexer_9 (.in0(1'b0), .in1(in_1[2]), .out(out_3[2]), .sel(_0_is_to_shift));
  Multiplexer #(.enable("false")) multiplexer_10 (.in0(in_1[2]), .in1(in_1[6]), .out(out_3[6]), .sel(_0_is_to_shift));
  Multiplexer #(.enable("false")) multiplexer_11 (.in0(in_1[6]), .in1(in_1[10]), .out(out_3[10]), .sel(_0_is_to_shift));
  Multiplexer #(.enable("false")) multiplexer_12 (
    .in0(in_1[10]), .in1(in_1[14]), .out(out_3[14]), .sel(_0_is_to_shift));
  Multiplexer #(.enable("false")) multiplexer_13 (.in0(1'b0), .in1(in_1[3]), .out(out_3[3]), .sel(_0_is_to_shift));
  Multiplexer #(.enable("false")) multiplexer_14 (.in0(in_1[3]), .in1(in_1[7]), .out(out_3[7]), .sel(_0_is_to_shift));
  Multiplexer #(.enable("false")) multiplexer_15 (.in0(in_1[7]), .in1(in_1[11]), .out(out_3[11]), .sel(_0_is_to_shift));
  Multiplexer #(.enable("false")) multiplexer_16 (
    .in0(in_1[11]), .in1(in_1[15]), .out(out_3[15]), .sel(_0_is_to_shift));

  // Other names for the same wires on the sheet: in0 = in_1[0]; in1 = in_1[1]; in2 = in_1[2]; in3 = in_1[3];
  //   in4 = in_1[4]; in5 = in_1[5]; in6 = in_1[6]; in7 = in_1[7]; in8 = in_1[8]; in9 = in_1[9]; in10 = in_1[10];
  //   in11 = in_1[11]; in12 = in_1[12]; in13 = in_1[13]; in14 = in_1[14]; in15 = in_1[15]; out0 = out_3[0];
  //   out1 = out_3[1]; out2 = out_3[2]; out3 = out_3[3]; out4 = out_3[4]; out5 = out_3[5]; out6 = out_3[6];
  //   out7 = out_3[7]; out8 = out_3[8]; out9 = out_3[9]; out10 = out_3[10]; out11 = out_3[11]; out12 = out_3[12];
  //   out13 = out_3[13]; out14 = out_3[14]; out15 = out_3[15]; select = _0_is_to_shift

  // Notes on the sheet:
  //   1 is not to shift
endmodule

module shl_barrel (
  input  [2:0] in_1,
  input  [15:0] in_2,
  output [15:0] out_3
);

  wire s1, s2, s4;
  wire [15:0] shl_1_bit_1_out_3, shl_2_bit_1_out_3;

  not not_1 (s1, in_1[0]);
  not not_2 (s2, in_1[1]);
  not not_3 (s4, in_1[2]);
  shl_1_bit shl_1_bit_1 (.in_1(in_2), ._0_is_to_shift(s1), .out_3(shl_1_bit_1_out_3));
  shl_2_bit shl_2_bit_1 (.in_1(shl_1_bit_1_out_3), ._0_is_to_shift(s2), .out_3(shl_2_bit_1_out_3));
  shl_4_bit shl_4_bit_1 (.in_1(shl_2_bit_1_out_3), ._0_is_to_shift(s4), .out_3(out_3));

  // Notes on the sheet:
  //   correct MUX behavior: 0 means no shift and 1 turns on shift
endmodule

module shra_1_bit (
  input  [15:0] in_1,
  input  in_2,
  output [15:0] out_3
);

  wire select;

  not not_1 (select, in_2);
  Multiplexer #(.enable("false")) multiplexer_1 (.in0(in_1[1]), .in1(in_1[0]), .out(out_3[0]), .sel(select));
  Multiplexer #(.enable("false")) multiplexer_2 (.in0(in_1[5]), .in1(in_1[4]), .out(out_3[4]), .sel(select));
  Multiplexer #(.enable("false")) multiplexer_3 (.in0(in_1[9]), .in1(in_1[8]), .out(out_3[8]), .sel(select));
  Multiplexer #(.enable("false")) multiplexer_4 (.in0(in_1[13]), .in1(in_1[12]), .out(out_3[12]), .sel(select));
  Multiplexer #(.enable("false")) multiplexer_5 (.in0(in_1[2]), .in1(in_1[1]), .out(out_3[1]), .sel(select));
  Multiplexer #(.enable("false")) multiplexer_6 (.in0(in_1[6]), .in1(in_1[5]), .out(out_3[5]), .sel(select));
  Multiplexer #(.enable("false")) multiplexer_7 (.in0(in_1[10]), .in1(in_1[9]), .out(out_3[9]), .sel(select));
  Multiplexer #(.enable("false")) multiplexer_8 (.in0(in_1[14]), .in1(in_1[13]), .out(out_3[13]), .sel(select));
  Multiplexer #(.enable("false")) multiplexer_9 (.in0(in_1[3]), .in1(in_1[2]), .out(out_3[2]), .sel(select));
  Multiplexer #(.enable("false")) multiplexer_10 (.in0(in_1[7]), .in1(in_1[6]), .out(out_3[6]), .sel(select));
  Multiplexer #(.enable("false")) multiplexer_11 (.in0(in_1[11]), .in1(in_1[10]), .out(out_3[10]), .sel(select));
  Multiplexer #(.enable("false")) multiplexer_12 (.in0(in_1[15]), .in1(in_1[14]), .out(out_3[14]), .sel(select));
  Multiplexer #(.enable("false")) multiplexer_13 (.in0(in_1[4]), .in1(in_1[3]), .out(out_3[3]), .sel(select));
  Multiplexer #(.enable("false")) multiplexer_14 (.in0(in_1[8]), .in1(in_1[7]), .out(out_3[7]), .sel(select));
  Multiplexer #(.enable("false")) multiplexer_15 (.in0(in_1[12]), .in1(in_1[11]), .out(out_3[11]), .sel(select));

  assign out_3[15] = in_1[15];

  // Other names for the same wires on the sheet: in0 = in_1[0]; in1 = in_1[1]; in2 = in_1[2]; in3 = in_1[3];
  //   in4 = in_1[4]; in5 = in_1[5]; in6 = in_1[6]; in7 = in_1[7]; in8 = in_1[8]; in9 = in_1[9]; in10 = in_1[10];
  //   in11 = in_1[11]; in12 = in_1[12]; in13 = in_1[13]; in14 = in_1[14]; out0 = out_3[0]; out1 = out_3[1];
  //   out2 = out_3[2]; out3 = out_3[3]; out4 = out_3[4]; out5 = out_3[5]; out6 = out_3[6]; out7 = out_3[7];
  //   out8 = out_3[8]; out9 = out_3[9]; out10 = out_3[10]; out11 = out_3[11]; out12 = out_3[12]; out13 = out_3[13];
  //   out14 = out_3[14]; in15 = in_1[15]

  // Notes on the sheet:
  //   1: shra is on
endmodule

module shra_2_bit (
  input  [15:0] in_1,
  input  in_2,
  output [15:0] out_3
);

  wire select;

  not not_1 (select, in_2);
  Multiplexer #(.enable("false")) multiplexer_1 (.in0(in_1[2]), .in1(in_1[0]), .out(out_3[0]), .sel(select));
  Multiplexer #(.enable("false")) multiplexer_2 (.in0(in_1[6]), .in1(in_1[4]), .out(out_3[4]), .sel(select));
  Multiplexer #(.enable("false")) multiplexer_3 (.in0(in_1[10]), .in1(in_1[8]), .out(out_3[8]), .sel(select));
  Multiplexer #(.enable("false")) multiplexer_4 (.in0(in_1[14]), .in1(in_1[12]), .out(out_3[12]), .sel(select));
  Multiplexer #(.enable("false")) multiplexer_5 (.in0(in_1[3]), .in1(in_1[1]), .out(out_3[1]), .sel(select));
  Multiplexer #(.enable("false")) multiplexer_6 (.in0(in_1[7]), .in1(in_1[5]), .out(out_3[5]), .sel(select));
  Multiplexer #(.enable("false")) multiplexer_7 (.in0(in_1[11]), .in1(in_1[9]), .out(out_3[9]), .sel(select));
  Multiplexer #(.enable("false")) multiplexer_8 (.in0(in_1[15]), .in1(in_1[13]), .out(out_3[13]), .sel(select));
  Multiplexer #(.enable("false")) multiplexer_9 (.in0(in_1[4]), .in1(in_1[2]), .out(out_3[2]), .sel(select));
  Multiplexer #(.enable("false")) multiplexer_10 (.in0(in_1[8]), .in1(in_1[6]), .out(out_3[6]), .sel(select));
  Multiplexer #(.enable("false")) multiplexer_11 (.in0(in_1[12]), .in1(in_1[10]), .out(out_3[10]), .sel(select));
  Multiplexer #(.enable("false")) multiplexer_12 (.in0(in_1[5]), .in1(in_1[3]), .out(out_3[3]), .sel(select));
  Multiplexer #(.enable("false")) multiplexer_13 (.in0(in_1[9]), .in1(in_1[7]), .out(out_3[7]), .sel(select));
  Multiplexer #(.enable("false")) multiplexer_14 (.in0(in_1[13]), .in1(in_1[11]), .out(out_3[11]), .sel(select));

  assign out_3[15:14] = {2{in_1[15]}};

  // Other names for the same wires on the sheet: in0 = in_1[0]; in1 = in_1[1]; in2 = in_1[2]; in3 = in_1[3];
  //   in4 = in_1[4]; in5 = in_1[5]; in6 = in_1[6]; in7 = in_1[7]; in8 = in_1[8]; in9 = in_1[9]; in10 = in_1[10];
  //   in11 = in_1[11]; in12 = in_1[12]; in13 = in_1[13]; in14 = in_1[14]; out0 = out_3[0]; out1 = out_3[1];
  //   out2 = out_3[2]; out3 = out_3[3]; out4 = out_3[4]; out5 = out_3[5]; out6 = out_3[6]; out7 = out_3[7];
  //   out8 = out_3[8]; out9 = out_3[9]; out10 = out_3[10]; out11 = out_3[11]; out12 = out_3[12]; out13 = out_3[13];
  //   in15 = in_1[15]

  // Notes on the sheet:
  //   1: shra is on
endmodule

module shra_4_bit (
  input  [15:0] in_1,
  input  in_2,
  output [15:0] out_3
);

  wire select;

  not not_1 (select, in_2);
  Multiplexer #(.enable("false")) multiplexer_1 (.in0(in_1[4]), .in1(in_1[0]), .out(out_3[0]), .sel(select));
  Multiplexer #(.enable("false")) multiplexer_2 (.in0(in_1[8]), .in1(in_1[4]), .out(out_3[4]), .sel(select));
  Multiplexer #(.enable("false")) multiplexer_3 (.in0(in_1[12]), .in1(in_1[8]), .out(out_3[8]), .sel(select));
  Multiplexer #(.enable("false")) multiplexer_4 (.in0(in_1[5]), .in1(in_1[1]), .out(out_3[1]), .sel(select));
  Multiplexer #(.enable("false")) multiplexer_5 (.in0(in_1[9]), .in1(in_1[5]), .out(out_3[5]), .sel(select));
  Multiplexer #(.enable("false")) multiplexer_6 (.in0(in_1[13]), .in1(in_1[9]), .out(out_3[9]), .sel(select));
  Multiplexer #(.enable("false")) multiplexer_7 (.in0(in_1[6]), .in1(in_1[2]), .out(out_3[2]), .sel(select));
  Multiplexer #(.enable("false")) multiplexer_8 (.in0(in_1[10]), .in1(in_1[6]), .out(out_3[6]), .sel(select));
  Multiplexer #(.enable("false")) multiplexer_9 (.in0(in_1[14]), .in1(in_1[10]), .out(out_3[10]), .sel(select));
  Multiplexer #(.enable("false")) multiplexer_10 (.in0(in_1[7]), .in1(in_1[3]), .out(out_3[3]), .sel(select));
  Multiplexer #(.enable("false")) multiplexer_11 (.in0(in_1[11]), .in1(in_1[7]), .out(out_3[7]), .sel(select));
  Multiplexer #(.enable("false")) multiplexer_12 (.in0(in_1[15]), .in1(in_1[11]), .out(out_3[11]), .sel(select));

  assign out_3[15:12] = {4{in_1[15]}};

  // Other names for the same wires on the sheet: in0 = in_1[0]; in1 = in_1[1]; in2 = in_1[2]; in3 = in_1[3];
  //   in4 = in_1[4]; in5 = in_1[5]; in6 = in_1[6]; in7 = in_1[7]; in8 = in_1[8]; in9 = in_1[9]; in10 = in_1[10];
  //   in11 = in_1[11]; in12 = in_1[12]; in13 = in_1[13]; in14 = in_1[14]; out0 = out_3[0]; out1 = out_3[1];
  //   out2 = out_3[2]; out3 = out_3[3]; out4 = out_3[4]; out5 = out_3[5]; out6 = out_3[6]; out7 = out_3[7];
  //   out8 = out_3[8]; out9 = out_3[9]; out10 = out_3[10]; out11 = out_3[11]; in15 = in_1[15]

  // Notes on the sheet:
  //   1: shra is on
endmodule

module shra_barrel (
  input  [2:0] in_1,
  input  [15:0] in_2,
  output [15:0] out_3
);

  wire [15:0] shra_1_bit_1_out_3, shra_2_bit_1_out_3;

  shra_1_bit shra_1_bit_1 (.in_1(in_2), .in_2(in_1[0]), .out_3(shra_1_bit_1_out_3));
  shra_2_bit shra_2_bit_1 (.in_1(shra_1_bit_1_out_3), .in_2(in_1[1]), .out_3(shra_2_bit_1_out_3));
  shra_4_bit shra_4_bit_1 (.in_1(shra_2_bit_1_out_3), .in_2(in_1[2]), .out_3(out_3));

  // Other names for the same wires on the sheet: s1 = in_1[0]; s2 = in_1[1]; s4 = in_1[2]
endmodule
